# Fritzing sketch wiring (saved by Fritzing 0.9.3b)

parts:
  Raspberry_Pi_1 = Raspberry Pi 3 [part_number=RPI-3-V1.2]
  Arduino = Arduino Nano (Rev3.0) (ICSP)
  Left_bumper = Pushbutton [package=THT]
  Right_bumper = Pushbutton [package=THT]
  Motor_driver = Motor Driver 1A Dual TB6612FNG
  Part3 = Logic Level Converter
  DC_Mot_Enc1 = DC Motor with two-phase hall-encoder [part_number=VT-E-G25A-06-177E]
  DC_Mot_Enc2 = DC Motor with two-phase hall-encoder [part_number=VT-E-G25A-06-177E]
  X1 = USB Connectors [package=s4b-ph]
  X2 = USB Connectors [package=s4b-ph]

nets:
  N1: Raspberry_Pi_1.GIPO17, Left_bumper.leg1
  N2: Raspberry_Pi_1.GIPO27, Right_bumper.leg1
  GND: Raspberry_Pi_1.GND, Left_bumper.leg0, Right_bumper.leg0, Motor_driver.GND, Part3.GND, DC_Mot_Enc1.pin5, DC_Mot_Enc2.pin5, X1.GND, X2.GND
  N3: Raspberry_Pi_1.GIPO15, Part3.RX2_LV
  N4: Raspberry_Pi_1.GIPO14, Part3.RX_LV
  5V: Raspberry_Pi_1.5V, Arduino.VIN, Motor_driver.VCC, Part3.HV, DC_Mot_Enc1.pin2, DC_Mot_Enc2.pin2, X2.D+
  N5: Arduino.D1/TX, Part3.RX2_HV
  N6: Arduino.D0/RX, Part3.RX_HV
  N7: Arduino.D2, DC_Mot_Enc1.pin3
  N8: Arduino.D3, DC_Mot_Enc2.pin3
  N9: Arduino.D5, Motor_driver.PWMA
  N10: Arduino.D6, Motor_driver.PWMB
  N11: Arduino.D9, Motor_driver.AIN1
  N12: Arduino.D10, Motor_driver.AIN2
  N13: Arduino.D11/MOSI, Motor_driver.BIN1
  N14: Arduino.D12/MISO, Motor_driver.BIN2
  N15: Arduino.A2, Motor_driver.STBY
  3.3V: Arduino.3V3, Part3.LV
  N16: Motor_driver.B01, DC_Mot_Enc2.pin1
  N17: Motor_driver.B02, DC_Mot_Enc2.pin6
  N18: Motor_driver.A02, DC_Mot_Enc1.pin1
  N19: Motor_driver.A01, DC_Mot_Enc1.pin6
  N20: Motor_driver.VM, X1.D+
  N21: X1.D-, X1.VBUS
  N22: X2.D-, X2.VBUS
